# Fritzing sketch Anschlüsse (saved by Fritzing 0.9.3b)
breadboards: 1

parts:
  Bauteil1 = Arduino Uno (Rev3)
  LCD1 = LCD screen
  R1 = Rotary Potentiometer (Small) [maximum_resistance=10kΩ package=THT]
  S1 = Pushbutton [package="[THT]"]
  R2 = Resistor [tolerance=±5% resistance=10k package=THT]

nets:
  N1: Bauteil1.D8, LCD1.E
  N2: Bauteil1.D9_PWM, LCD1.DB4
  N3: Bauteil1.D10_PWM/SS, LCD1.DB5
  N4: Bauteil1.D11_PWM/MOSI, LCD1.DB6
  N5: Bauteil1.D12/MISO, LCD1.DB7
  GND: Bauteil1.GND, LCD1.VSS, LCD1.R/W, LCD1.LED-, R1.leg1, R2.Pin_1
  N6: Bauteil1.D7, LCD1.RS
  5V: Bauteil1.5V, LCD1.VDD, LCD1.LED+, R1.leg2, S1.Pin_3, S1.Pin_4
  N7: LCD1.V0, R1.wiper
  N8: S1.Pin_1, S1.Pin_2, R2.Pin_0
